// Logisim project And.circ as structural Verilog: 1 circuit, main circuit main
module main (
);

  wire dipswitch_1_p1, dipswitch_1_p2, nand_1_out, not_1_out;

  // DipSwitch #(.number(2)) dipswitch_1: pin names not known; wires that end beside it: dipswitch_1_p1, dipswitch_1_p2
  nand nand_1 (nand_1_out, dipswitch_1_p1, dipswitch_1_p2);
  not not_1 (not_1_out, nand_1_out);
  LED led_1 (.in(not_1_out));
endmodule
