// Logisim project And16.circ as structural Verilog: 1 circuit, main circuit main
module main (
);

  wire and_1_out, and_2_out, and_3_out, and_4_out, and_5_out, and_6_out, and_7_out, and_8_out, and_9_out,
       and_10_out, and_11_out, and_12_out, and_13_out, and_14_out, and_15_out, dipswitch_1_p1,
       dipswitch_1_p2, dipswitch_1_p3, dipswitch_1_p4, dipswitch_1_p5, dipswitch_1_p6, dipswitch_1_p7,
       dipswitch_1_p8, dipswitch_1_p9, dipswitch_1_p10, dipswitch_1_p11, dipswitch_1_p12, dipswitch_1_p13,
       dipswitch_1_p14, dipswitch_1_p15, dipswitch_1_p16;

  // DipSwitch #(.number(17)) dipswitch_1: pin names not known; wires that end beside it: dipswitch_1_p1, dipswitch_1_p2, dipswitch_1_p3, dipswitch_1_p4, dipswitch_1_p5, dipswitch_1_p6, dipswitch_1_p7, dipswitch_1_p8, dipswitch_1_p9, dipswitch_1_p10, dipswitch_1_p11, dipswitch_1_p12, dipswitch_1_p13, dipswitch_1_p14, dipswitch_1_p15, dipswitch_1_p16
  and and_1 (and_1_out, dipswitch_1_p1, dipswitch_1_p2);
  LED led_1 (.in(and_15_out));
  and and_2 (and_2_out, and_1_out, dipswitch_1_p3);
  and and_3 (and_3_out, and_2_out, dipswitch_1_p4);
  and and_4 (and_4_out, and_3_out, dipswitch_1_p5);
  and and_5 (and_5_out, and_4_out, dipswitch_1_p6);
  and and_6 (and_6_out, and_5_out, dipswitch_1_p7);
  and and_7 (and_7_out, and_6_out, dipswitch_1_p8);
  and and_8 (and_8_out, and_7_out, dipswitch_1_p9);
  and and_9 (and_9_out, and_8_out, dipswitch_1_p10);
  and and_10 (and_10_out, and_9_out, dipswitch_1_p11);
  and and_11 (and_11_out, and_10_out, dipswitch_1_p12);
  and and_12 (and_12_out, and_11_out, dipswitch_1_p13);
  and and_13 (and_13_out, and_12_out, dipswitch_1_p14);
  and and_14 (and_14_out, and_13_out, dipswitch_1_p15);
  and and_15 (and_15_out, and_14_out, dipswitch_1_p16);

  // Notes on the sheet:
  //   E
endmodule
