// Logisim project Bit.circ as structural Verilog: 1 circuit, main circuit main
module main (
  input  Inp,
  input  load
);

  wire clock_1_out, d_ff_1_q, multiplexer_1_out;

  D_Flip_Flop d_ff_1 (.D(multiplexer_1_out), .clk(clock_1_out), .Q(d_ff_1_q));  // open: Qn, preset, reset
  Multiplexer multiplexer_1 (.in0(d_ff_1_q), .in1(Inp), .out(multiplexer_1_out), .sel(load));
  Clock clock_1 (.out(clock_1_out));
  LED led_1 (.in(d_ff_1_q));
endmodule
