// Logisim project CPU.circ as structural Verilog: 1 circuit, main circuit CPU_Hack
module CPU_Hack (
  input  [15:0] inM,
  input  [15:0] instruction,
  input  reset,
  output [15:0] outM,
  output [14:0] out_5,
  output [14:0] out_6
);

  wire and_1_out, and_2_out, and_3_out, cAorM, cDestA, cDestD, cDestM, cF, cJEQ, cJGT, cJLT, clk_out, cNO,
       cNX, cNY, cZX, cZY, loadA, negp, or_2_out, posp, zerop;
  wire [14:13] multiplexer_1_out;
  wire [15:0] dRegOut, multiplexer_2_out, yIn;
  wire [15:15] aRegOut, pc_1_outp;

  Multiplexer #(.width(16)) multiplexer_1 (
    .in0({16{1'b0}}), .in1(instruction),
    .out({instruction[15], multiplexer_1_out, cAorM, cZX, cNX, cZY, cNY, cF, cNO, cDestA, cDestD, cDestM, cJLT, cJEQ, cJGT}),
    .sel(instruction[15]));
  Clock #(.phaseOffset(4)) clk (.out(clk_out));
  Multiplexer #(.width(16)) multiplexer_2 (
    .in0(instruction), .in1(outM), .out(multiplexer_2_out), .sel(instruction[15]));
  Multiplexer #(.width(16)) multiplexer_3 (.in0({aRegOut[15], out_6}), .in1(inM), .out(yIn), .sel(cAorM));
  Reg A_register (.clck(clk_out), .inp(multiplexer_2_out), .load(loadA), .outp({aRegOut[15], out_6}));
  or or_1 (loadA, ~instruction[15], cDestA);  // OR_Gate
  and and_1 (and_1_out, cJLT, negp);
  and and_2 (and_2_out, cJEQ, zerop);
  and and_3 (and_3_out, cJGT, posp);
  or or_2 (or_2_out, and_1_out, and_2_out, and_3_out);
  Reg D_register (.clck(clk_out), .inp(outM), .load(cDestD), .outp(dRegOut));
  ALU alu_1 (
    .X(dRegOut), .NO(cNO), .ZX(cZX), .NX(cNX), .Y(yIn), .F(cF), .ZY(cZY), .NY(cNY), .out_9(outM), .NG(zerop),
    .ZR(negp));
  LED writeM (.in(cDestM));
  PC pc_1 (
    .inpt({aRegOut[15], out_6}), .clck(clk_out), .load(or_2_out), .inc(1'b1), .rst(reset),
    .outp({pc_1_outp[15], out_5}));
  // LedBar #(.inputtype("row"), .matrixcols(15)) pcOut: pin names not known; wires that end beside it: out_5
  // LedBar #(.inputtype("row"), .matrixcols(15)) addressM: pin names not known; wires that end beside it: out_6
  and and_4 (posp, ~zerop, ~negp);  // AND_Gate

  // Other names for the same wires on the sheet: aInput[15:0] = instruction; cType = instruction[15];
  //   aluOut[15:0] = outM; aRegOut[14:0] = out_6

  // Notes on the sheet:
  //   HACK - CPU
endmodule
