// Logisim project DMux.circ as structural Verilog: 1 circuit, main circuit main
module main (
);

  wire and_1_out, and_2_out, dipswitch_1_p1, dipswitch_1_p2, not_1_out, sel_out;

  // DipSwitch #(.number(2)) dipswitch_1: pin names not known; wires that end beside it: dipswitch_1_p1, dipswitch_1_p2
  Button sel (.out(sel_out));
  not not_1 (not_1_out, sel_out);
  and and_1 (and_1_out, dipswitch_1_p2, not_1_out);
  and and_2 (and_2_out, sel_out, dipswitch_1_p1);
  LED led_1 (.in(and_1_out));
  LED led_2 (.in(and_2_out));
endmodule
