// Logisim project DMux4Way.circ as structural Verilog: 1 circuit, main circuit main
module main (
  input  [1:0] in_1
);

  wire demultiplexer_1_out0, demultiplexer_1_out1, demultiplexer_2_out0, demultiplexer_2_out1,
       demultiplexer_3_out0, demultiplexer_3_out1, Inp_out;

  Button Inp (.out(Inp_out));
  Demultiplexer demultiplexer_1 (.out0(demultiplexer_1_out0), .out1(demultiplexer_1_out1), .in(Inp_out), .sel(in_1[1]));
  Demultiplexer demultiplexer_2 (
    .out0(demultiplexer_2_out0), .out1(demultiplexer_2_out1), .in(demultiplexer_1_out0), .sel(in_1[0]));
  Demultiplexer demultiplexer_3 (
    .out0(demultiplexer_3_out0), .out1(demultiplexer_3_out1), .in(demultiplexer_1_out1), .sel(in_1[0]));
  LED led_1 (.in(demultiplexer_2_out0));
  LED led_2 (.in(demultiplexer_2_out1));
  LED led_3 (.in(demultiplexer_3_out0));
  LED led_4 (.in(demultiplexer_3_out1));

  // Notes on the sheet:
  //   in_1: initial=0x2
endmodule
