// Logisim project FullAdder.circ as structural Verilog: 1 circuit, main circuit main
module main (
);

  wire adder_1_cout, adder_1_out, adder_2_cout, adder_2_out, dipswitch_1_p1, dipswitch_1_p2, dipswitch_1_p3,
       or_1_out;

  // DipSwitch #(.number(3)) dipswitch_1: pin names not known; wires that end beside it: dipswitch_1_p1, dipswitch_1_p2, dipswitch_1_p3
  Adder #(.width(1)) adder_1 (
    .a(dipswitch_1_p1), .b(dipswitch_1_p2), .out(adder_1_out), .cout(adder_1_cout));  // open: cin
  Adder #(.width(1)) adder_2 (
    .a(adder_1_out), .b(dipswitch_1_p3), .out(adder_2_out), .cout(adder_2_cout));  // open: cin
  LED led_1 (.in(adder_2_out));
  or or_1 (or_1_out, adder_2_cout, adder_1_cout);
  LED led_2 (.in(or_1_out));

  // Notes on the sheet:
  //   Sum
  //   Carry
endmodule
