// Logisim project HalfAdder.circ as structural Verilog: 1 circuit, main circuit main
module main (
);

  wire and_1_out, dipswitch_1_sw1, dipswitch_1_sw2, xor_1_out;

  DipSwitch #(.number(2)) dipswitch_1 (.sw1(dipswitch_1_sw1), .sw2(dipswitch_1_sw2));
  xor xor_1 (xor_1_out, dipswitch_1_sw1, dipswitch_1_sw2);
  LED led_1 (.in(xor_1_out));
  and and_1 (and_1_out, dipswitch_1_sw1, dipswitch_1_sw2);
  LED led_2 (.in(and_1_out));

  // Notes on the sheet:
  //   Sum
  //   Carry
endmodule
