// Logisim project Mux.circ as structural Verilog: 1 circuit, main circuit main
module main (
);

  wire and_1_out, and_2_out, dipswitch_1_sw1, dipswitch_1_sw2, not_1_out, or_1_out, sel_out;

  DipSwitch #(.number(2)) dipswitch_1 (.sw1(dipswitch_1_sw1), .sw2(dipswitch_1_sw2));
  not not_1 (not_1_out, sel_out);
  Button sel (.out(sel_out));
  and and_1 (and_1_out, dipswitch_1_sw1, not_1_out);
  and and_2 (and_2_out, sel_out, dipswitch_1_sw2);
  or or_1 (or_1_out, and_1_out, and_2_out);
  LED led_1 (.in(or_1_out));
endmodule
