// Logisim project Mux16.circ as structural Verilog: 1 circuit, main circuit main
module main (
);

  wire multiplexer_1_out, multiplexer_2_out, multiplexer_3_out, multiplexer_4_out, multiplexer_5_out;
  wire [1:0] dipswitch_5_sw2, dipswitch_6_sw2;

  // DipSwitch #(.number(4)) dipswitch_1: pin names not known
  // DipSwitch #(.number(4)) dipswitch_2: pin names not known
  // DipSwitch #(.number(4)) dipswitch_3: pin names not known
  // DipSwitch #(.number(4)) dipswitch_4: pin names not known
  Multiplexer #(.select(2)) multiplexer_1 (.out(multiplexer_1_out), .sel(dipswitch_5_sw2));  // open: in0, in1, in2, in3
  Multiplexer #(.select(2)) multiplexer_2 (.out(multiplexer_2_out), .sel(dipswitch_5_sw2));  // open: in0, in1, in2, in3
  Multiplexer #(.select(2)) multiplexer_3 (.out(multiplexer_3_out), .sel(dipswitch_5_sw2));  // open: in0, in1, in2, in3
  Multiplexer #(.select(2)) multiplexer_4 (.out(multiplexer_4_out), .sel(dipswitch_5_sw2));  // open: in0, in1, in2, in3
  DipSwitch #(.number(2)) dipswitch_5 (.sw1(dipswitch_5_sw2[1]), .sw2(dipswitch_5_sw2[0]));
  Multiplexer #(.select(2)) multiplexer_5 (
    .in0(multiplexer_1_out), .in1(multiplexer_2_out), .in2(multiplexer_3_out), .in3(multiplexer_4_out),
    .out(multiplexer_5_out), .sel(dipswitch_6_sw2));
  DipSwitch #(.number(2)) dipswitch_6 (.sw1(dipswitch_6_sw2[1]), .sw2(dipswitch_6_sw2[0]));
  LED led_1 (.in(multiplexer_5_out));
endmodule
