// Logisim project Not.circ as structural Verilog: 1 circuit, main circuit main
module main (
);

  wire A_out, nand_1_out;

  Button A (.out(A_out));
  nand nand_1 (nand_1_out, A_out, A_out);
  LED led_1 (.in(nand_1_out));
endmodule
