// Logisim project Not16.circ as structural Verilog: 1 circuit, main circuit main
module main (
);

  wire dipswitch_1_p1, dipswitch_1_p2, dipswitch_1_p3, dipswitch_1_p4, dipswitch_1_p5, dipswitch_1_p6,
       dipswitch_1_p7, dipswitch_1_p8, not_1_out;

  // DipSwitch dipswitch_1: pin names not known; wires that end beside it: dipswitch_1_p1, dipswitch_1_p2, dipswitch_1_p3, dipswitch_1_p4, dipswitch_1_p5, dipswitch_1_p6, dipswitch_1_p7, dipswitch_1_p8
  not not_1 (not_1_out, dipswitch_1_p1);
  not not_2 (not_1_out, dipswitch_1_p2);
  not not_3 (not_1_out, dipswitch_1_p3);
  not not_4 (not_1_out, dipswitch_1_p4);
  not not_5 (not_1_out, dipswitch_1_p5);
  not not_6 (not_1_out, dipswitch_1_p6);
  not not_7 (not_1_out, dipswitch_1_p7);
  not not_8 (not_1_out, dipswitch_1_p8);
  LED led_1 (.in(not_1_out));
endmodule
