// Logisim project Or.circ as structural Verilog: 1 circuit, main circuit main
module main (
);

  wire dipswitch_1_sw1, dipswitch_1_sw2, nand_1_out, nand_2_out, nand_3_out;

  DipSwitch #(.number(2)) dipswitch_1 (.sw1(dipswitch_1_sw1), .sw2(dipswitch_1_sw2));
  nand nand_1 (nand_1_out, dipswitch_1_sw1, dipswitch_1_sw1);
  nand nand_2 (nand_2_out, dipswitch_1_sw2, dipswitch_1_sw2);
  nand nand_3 (nand_3_out, nand_1_out, nand_2_out);
  LED led_1 (.in(nand_3_out));
endmodule
