// Logisim project Or16.circ as structural Verilog: 1 circuit, main circuit main
module main (
);

  wire dipswitch_1_p1, dipswitch_1_p2, dipswitch_1_p3, dipswitch_1_p4, dipswitch_1_p5, dipswitch_1_p6,
       dipswitch_1_p7, dipswitch_1_p8, dipswitch_1_p9, dipswitch_1_p10, dipswitch_1_p11, dipswitch_1_p12,
       dipswitch_1_p13, dipswitch_1_p14, dipswitch_1_p15, dipswitch_1_p16, or_1_out, or_2_out, or_3_out,
       or_4_out, or_5_out, or_6_out, or_7_out, or_8_out, or_9_out, or_10_out, or_11_out, or_12_out,
       or_13_out, or_14_out, or_15_out;

  LED led_1 (.in(or_14_out));
  // DipSwitch #(.number(16)) dipswitch_1: pin names not known; wires that end beside it: dipswitch_1_p1, dipswitch_1_p2, dipswitch_1_p3, dipswitch_1_p4, dipswitch_1_p5, dipswitch_1_p6, dipswitch_1_p7, dipswitch_1_p8, dipswitch_1_p9, dipswitch_1_p10, dipswitch_1_p11, dipswitch_1_p12, dipswitch_1_p13, dipswitch_1_p14, dipswitch_1_p15, dipswitch_1_p16
  or or_1 (or_1_out, dipswitch_1_p1, dipswitch_1_p2);
  or or_2 (or_2_out, dipswitch_1_p10, dipswitch_1_p9);
  or or_3 (or_3_out, or_1_out, dipswitch_1_p3);
  or or_4 (or_4_out, or_3_out, dipswitch_1_p4);
  or or_5 (or_5_out, dipswitch_1_p12, or_6_out);
  or or_6 (or_6_out, dipswitch_1_p11, or_2_out);
  or or_7 (or_7_out, or_4_out, dipswitch_1_p5);
  or or_8 (or_8_out, or_7_out, dipswitch_1_p6);
  or or_9 (or_9_out, dipswitch_1_p14, or_10_out);
  or or_10 (or_10_out, dipswitch_1_p13, or_5_out);
  or or_11 (or_11_out, or_8_out, dipswitch_1_p7);
  or or_12 (or_12_out, dipswitch_1_p15, or_9_out);
  or or_13 (or_13_out, or_11_out, dipswitch_1_p8);
  or or_14 (or_14_out, or_13_out, or_15_out);
  or or_15 (or_15_out, dipswitch_1_p16, or_12_out);
endmodule
