// Logisim project Or8Way.circ as structural Verilog: 1 circuit, main circuit main
module main (
);

  wire dipswitch_1_p1, dipswitch_1_p2, dipswitch_1_p3, dipswitch_1_p4, dipswitch_1_p5, dipswitch_1_p6,
       dipswitch_1_p7, dipswitch_1_p8, or_1_out, or_2_out, or_3_out, or_4_out, or_5_out, or_6_out, or_7_out;

  // DipSwitch dipswitch_1: pin names not known; wires that end beside it: dipswitch_1_p1, dipswitch_1_p2, dipswitch_1_p3, dipswitch_1_p4, dipswitch_1_p5, dipswitch_1_p6, dipswitch_1_p7, dipswitch_1_p8
  or or_1 (or_1_out, dipswitch_1_p1, dipswitch_1_p2);
  or or_2 (or_2_out, dipswitch_1_p7, dipswitch_1_p8);
  or or_3 (or_3_out, or_1_out, dipswitch_1_p3);
  or or_4 (or_4_out, or_3_out, dipswitch_1_p4);
  or or_5 (or_5_out, dipswitch_1_p5, or_6_out);
  or or_6 (or_6_out, dipswitch_1_p6, or_2_out);
  or or_7 (or_7_out, or_4_out, or_5_out);
  LED led_1 (.in(or_7_out));
endmodule
