// Logisim project PC.circ as structural Verilog: 1 circuit, main circuit main
module main (
  input  [15:0] in_1,
  input  clck,
  input  load,
  input  inc,
  input  rst,
  output [15:0] out_6
);

  wire multiplexer_4_out, multiplexer_5_out, multiplexer_6_out, multiplexer_7_out, multiplexer_8_out,
       multiplexer_9_out, multiplexer_10_out, multiplexer_11_out, multiplexer_12_out, multiplexer_13_out,
       multiplexer_14_out, multiplexer_15_out, multiplexer_16_out, multiplexer_17_out, multiplexer_18_out,
       multiplexer_19_out;
  wire [15:0] adder_1_out, multiplexer_1_out, multiplexer_2_out, multiplexer_3_out;

  Multiplexer #(.width(16)) multiplexer_1 (.in0(multiplexer_3_out), .in1(in_1), .out(multiplexer_1_out), .sel(load));
  Multiplexer #(.width(16)) multiplexer_2 (
    .in0(multiplexer_1_out), .in1({16{1'b0}}), .out(multiplexer_2_out), .sel(rst));
  Multiplexer #(.width(16)) multiplexer_3 (.in0(out_6), .in1(adder_1_out), .out(multiplexer_3_out), .sel(inc));
  Adder #(.width(16)) adder_1 (.a(out_6), .b(16'h1), .out(adder_1_out));  // open: cin, cout
  Multiplexer multiplexer_4 (.in0(out_6[0]), .in1(multiplexer_2_out[0]), .out(multiplexer_4_out), .sel(1'b1));
  Multiplexer multiplexer_5 (.in0(out_6[1]), .in1(multiplexer_2_out[1]), .out(multiplexer_5_out), .sel(1'b1));
  Multiplexer multiplexer_6 (.in0(out_6[2]), .in1(multiplexer_2_out[2]), .out(multiplexer_6_out), .sel(1'b1));
  Multiplexer multiplexer_7 (.in0(out_6[3]), .in1(multiplexer_2_out[3]), .out(multiplexer_7_out), .sel(1'b1));
  Multiplexer multiplexer_8 (.in0(out_6[4]), .in1(multiplexer_2_out[4]), .out(multiplexer_8_out), .sel(1'b1));
  Multiplexer multiplexer_9 (.in0(out_6[5]), .in1(multiplexer_2_out[5]), .out(multiplexer_9_out), .sel(1'b1));
  Multiplexer multiplexer_10 (.in0(out_6[6]), .in1(multiplexer_2_out[6]), .out(multiplexer_10_out), .sel(1'b1));
  Multiplexer multiplexer_11 (.in0(out_6[7]), .in1(multiplexer_2_out[7]), .out(multiplexer_11_out), .sel(1'b1));
  Multiplexer multiplexer_12 (.in0(out_6[8]), .in1(multiplexer_2_out[8]), .out(multiplexer_12_out), .sel(1'b1));
  Multiplexer multiplexer_13 (.in0(out_6[9]), .in1(multiplexer_2_out[9]), .out(multiplexer_13_out), .sel(1'b1));
  Multiplexer multiplexer_14 (.in0(out_6[10]), .in1(multiplexer_2_out[10]), .out(multiplexer_14_out), .sel(1'b1));
  Multiplexer multiplexer_15 (.in0(out_6[11]), .in1(multiplexer_2_out[11]), .out(multiplexer_15_out), .sel(1'b1));
  Multiplexer multiplexer_16 (.in0(out_6[12]), .in1(multiplexer_2_out[12]), .out(multiplexer_16_out), .sel(1'b1));
  Multiplexer multiplexer_17 (.in0(out_6[13]), .in1(multiplexer_2_out[13]), .out(multiplexer_17_out), .sel(1'b1));
  Multiplexer multiplexer_18 (.in0(out_6[14]), .in1(multiplexer_2_out[14]), .out(multiplexer_18_out), .sel(1'b1));
  Multiplexer multiplexer_19 (.in0(out_6[15]), .in1(multiplexer_2_out[15]), .out(multiplexer_19_out), .sel(1'b1));
  D_Flip_Flop d_ff_1 (.D(multiplexer_4_out), .clk(clck), .Q(out_6[0]));  // open: Qn, preset, reset
  D_Flip_Flop d_ff_2 (.D(multiplexer_5_out), .clk(clck), .Q(out_6[1]));  // open: Qn, preset, reset
  D_Flip_Flop d_ff_3 (.D(multiplexer_6_out), .clk(clck), .Q(out_6[2]));  // open: Qn, preset, reset
  D_Flip_Flop d_ff_4 (.D(multiplexer_7_out), .clk(clck), .Q(out_6[3]));  // open: Qn, preset, reset
  D_Flip_Flop d_ff_5 (.D(multiplexer_8_out), .clk(clck), .Q(out_6[4]));  // open: Qn, preset, reset
  D_Flip_Flop d_ff_6 (.D(multiplexer_9_out), .clk(clck), .Q(out_6[5]));  // open: Qn, preset, reset
  D_Flip_Flop d_ff_7 (.D(multiplexer_10_out), .clk(clck), .Q(out_6[6]));  // open: Qn, preset, reset
  D_Flip_Flop d_ff_8 (.D(multiplexer_11_out), .clk(clck), .Q(out_6[7]));  // open: Qn, preset, reset
  D_Flip_Flop d_ff_9 (.D(multiplexer_12_out), .clk(clck), .Q(out_6[8]));  // open: Qn, preset, reset
  D_Flip_Flop d_ff_10 (.D(multiplexer_13_out), .clk(clck), .Q(out_6[9]));  // open: Qn, preset, reset
  D_Flip_Flop d_ff_11 (.D(multiplexer_14_out), .clk(clck), .Q(out_6[10]));  // open: Qn, preset, reset
  D_Flip_Flop d_ff_12 (.D(multiplexer_15_out), .clk(clck), .Q(out_6[11]));  // open: Qn, preset, reset
  D_Flip_Flop d_ff_13 (.D(multiplexer_16_out), .clk(clck), .Q(out_6[12]));  // open: Qn, preset, reset
  D_Flip_Flop d_ff_14 (.D(multiplexer_17_out), .clk(clck), .Q(out_6[13]));  // open: Qn, preset, reset
  D_Flip_Flop d_ff_15 (.D(multiplexer_18_out), .clk(clck), .Q(out_6[14]));  // open: Qn, preset, reset
  D_Flip_Flop d_ff_16 (.D(multiplexer_19_out), .clk(clck), .Q(out_6[15]));  // open: Qn, preset, reset
endmodule
