// Logisim project RAM16K.circ as structural Verilog: 1 circuit, main circuit mainRAM16K
module mainRAM16K (
  input  [15:0] inpt,
  input  clck,
  input  load,
  input  [13:0] address,
  output [15:0] outp
);

  wire clock_1_out, demultiplexer_1_out0, demultiplexer_1_out1, demultiplexer_1_out2, demultiplexer_1_out3;
  wire [15:0] mainram4k_1_outp, mainram4k_2_outp, mainram4k_3_outp, mainram4k_4_outp;

  Demultiplexer #(.select(2)) demultiplexer_1 (
    .out0(demultiplexer_1_out0), .out1(demultiplexer_1_out1), .out2(demultiplexer_1_out2),
    .out3(demultiplexer_1_out3), .in(load), .sel(address[13:12]));
  Clock clock_1 (.out(clock_1_out));
  mainRAM4k mainram4k_1 (
    .inpt(inpt), .clck(clock_1_out), .load(demultiplexer_1_out0), .address(address[11:0]),
    .outp(mainram4k_1_outp));
  mainRAM4k mainram4k_2 (
    .inpt(inpt), .clck(clock_1_out), .load(demultiplexer_1_out1), .address(address[11:0]),
    .outp(mainram4k_2_outp));
  mainRAM4k mainram4k_3 (
    .inpt(inpt), .clck(clock_1_out), .load(demultiplexer_1_out2), .address(address[11:0]),
    .outp(mainram4k_3_outp));
  mainRAM4k mainram4k_4 (
    .inpt(inpt), .clck(clock_1_out), .load(demultiplexer_1_out3), .address(address[11:0]),
    .outp(mainram4k_4_outp));
  Multiplexer #(.select(2), .width(16)) multiplexer_1 (
    .in0(mainram4k_1_outp), .in1(mainram4k_2_outp), .in2(mainram4k_3_outp), .in3(mainram4k_4_outp),
    .out(outp), .sel(address[13:12]));

  // Other names for the same wires on the sheet: address_t[1:0] = address[13:12]
endmodule
