// Logisim project RAM4K.circ as structural Verilog: 1 circuit, main circuit mainRAM4k
module mainRAM4k (
  input  [15:0] inpt,
  input  clck,
  input  load,
  input  [11:0] address,
  output [15:0] outp
);

  wire demultiplexer_1_out0, demultiplexer_1_out1, demultiplexer_1_out2, demultiplexer_1_out3,
       demultiplexer_1_out4, demultiplexer_1_out5, demultiplexer_1_out6, demultiplexer_1_out7;
  wire [15:0] mainram512_1_outp, mainram512_2_outp, mainram512_3_outp, mainram512_4_outp, mainram512_5_outp,
       mainram512_6_outp, mainram512_7_outp, mainram512_8_outp;

  Demultiplexer #(.select(3)) demultiplexer_1 (
    .out0(demultiplexer_1_out0), .out1(demultiplexer_1_out1), .out2(demultiplexer_1_out2),
    .out3(demultiplexer_1_out3), .out4(demultiplexer_1_out4), .out5(demultiplexer_1_out5),
    .out6(demultiplexer_1_out6), .out7(demultiplexer_1_out7), .in(load), .sel(address[2:0]));
  mainRAM512 mainram512_1 (
    .clck(clck), .inpt(inpt), .load(demultiplexer_1_out0), .address(address[11:3]), .outp(mainram512_1_outp));
  mainRAM512 mainram512_2 (
    .clck(clck), .inpt(inpt), .load(demultiplexer_1_out1), .address(address[11:3]), .outp(mainram512_2_outp));
  mainRAM512 mainram512_3 (
    .clck(clck), .inpt(inpt), .load(demultiplexer_1_out2), .address(address[11:3]), .outp(mainram512_3_outp));
  mainRAM512 mainram512_4 (
    .clck(clck), .inpt(inpt), .load(demultiplexer_1_out3), .address(address[11:3]), .outp(mainram512_4_outp));
  mainRAM512 mainram512_5 (
    .clck(clck), .inpt(inpt), .load(demultiplexer_1_out4), .address(address[11:3]), .outp(mainram512_5_outp));
  mainRAM512 mainram512_6 (
    .clck(clck), .inpt(inpt), .load(demultiplexer_1_out5), .address(address[11:3]), .outp(mainram512_6_outp));
  mainRAM512 mainram512_7 (
    .clck(clck), .inpt(inpt), .load(demultiplexer_1_out6), .address(address[11:3]), .outp(mainram512_7_outp));
  mainRAM512 mainram512_8 (
    .clck(clck), .inpt(inpt), .load(demultiplexer_1_out7), .address(address[11:3]), .outp(mainram512_8_outp));
  Multiplexer #(.select(3), .width(16)) multiplexer_1 (
    .in0(mainram512_1_outp), .in1(mainram512_2_outp), .in2(mainram512_3_outp), .in3(mainram512_4_outp),
    .in4(mainram512_5_outp), .in5(mainram512_6_outp), .in6(mainram512_7_outp), .in7(mainram512_8_outp),
    .out(outp), .sel(address[2:0]));

  // Other names for the same wires on the sheet: address_t[2:0] = address[2:0]
endmodule
