// Logisim project RAM512.circ as structural Verilog: 1 circuit, main circuit mainRAM512
module mainRAM512 (
  input  clck,
  input  [15:0] inpt,
  input  load,
  input  [8:0] address,
  output [15:0] outp
);

  wire demultiplexer_1_out0, demultiplexer_1_out1, demultiplexer_1_out2, demultiplexer_1_out3,
       demultiplexer_1_out4, demultiplexer_1_out5, demultiplexer_1_out6, demultiplexer_1_out7;
  wire [15:0] ram64_1_out_5, ram64_2_out_5, ram64_3_out_5, ram64_4_out_5, ram64_5_out_5, ram64_6_out_5,
       ram64_7_out_5, ram64_8_out_5;

  Demultiplexer #(.select(3)) demultiplexer_1 (
    .out0(demultiplexer_1_out0), .out1(demultiplexer_1_out1), .out2(demultiplexer_1_out2),
    .out3(demultiplexer_1_out3), .out4(demultiplexer_1_out4), .out5(demultiplexer_1_out5),
    .out6(demultiplexer_1_out6), .out7(demultiplexer_1_out7), .in(load), .sel(address[2:0]));
  RAM64 ram64_1 (.clck(clck), .load(demultiplexer_1_out0), .inp(inpt), .address(address[8:3]), .out_5(ram64_1_out_5));
  RAM64 ram64_2 (.clck(clck), .load(demultiplexer_1_out1), .inp(inpt), .address(address[8:3]), .out_5(ram64_2_out_5));
  RAM64 ram64_3 (.clck(clck), .load(demultiplexer_1_out2), .inp(inpt), .address(address[8:3]), .out_5(ram64_3_out_5));
  RAM64 ram64_4 (.clck(clck), .load(demultiplexer_1_out3), .inp(inpt), .address(address[8:3]), .out_5(ram64_4_out_5));
  RAM64 ram64_5 (.clck(clck), .load(demultiplexer_1_out4), .inp(inpt), .address(address[8:3]), .out_5(ram64_5_out_5));
  RAM64 ram64_6 (.clck(clck), .load(demultiplexer_1_out5), .inp(inpt), .address(address[8:3]), .out_5(ram64_6_out_5));
  RAM64 ram64_7 (.clck(clck), .load(demultiplexer_1_out6), .inp(inpt), .address(address[8:3]), .out_5(ram64_7_out_5));
  RAM64 ram64_8 (.clck(clck), .load(demultiplexer_1_out7), .inp(inpt), .address(address[8:3]), .out_5(ram64_8_out_5));
  Multiplexer #(.select(3), .width(16)) multiplexer_1 (
    .in0(ram64_1_out_5), .in1(ram64_2_out_5), .in2(ram64_3_out_5), .in3(ram64_4_out_5), .in4(ram64_5_out_5),
    .in5(ram64_6_out_5), .in6(ram64_7_out_5), .in7(ram64_8_out_5), .out(outp), .sel(address[2:0]));

  // Other names for the same wires on the sheet: address_t[2:0] = address[2:0]
endmodule
