// Logisim project RAM64.circ as structural Verilog: 1 circuit, main circuit RAM64
module RAM64 (
  input  clck,
  input  load,
  input  [15:0] inp,
  input  [5:0] address,
  output [15:0] out_5
);

  wire demultiplexer_1_out0, demultiplexer_1_out1, demultiplexer_1_out2, demultiplexer_1_out3,
       demultiplexer_1_out4, demultiplexer_1_out5, demultiplexer_1_out6, demultiplexer_1_out7;
  wire [15:0] main1_1_outp, main1_2_outp, main1_3_outp, main1_4_outp, main1_5_outp, main1_6_outp,
       main1_7_outp, RAM8_outp;

  Demultiplexer #(.select(3)) demultiplexer_1 (
    .out0(demultiplexer_1_out0), .out1(demultiplexer_1_out1), .out2(demultiplexer_1_out2),
    .out3(demultiplexer_1_out3), .out4(demultiplexer_1_out4), .out5(demultiplexer_1_out5),
    .out6(demultiplexer_1_out6), .out7(demultiplexer_1_out7), .in(load), .sel(address[2:0]));
  main1 RAM8 (.clck(clck), .inp(inp), .load(demultiplexer_1_out0), .address(address[5:3]), .outp(RAM8_outp));
  main1 main1_1 (.clck(clck), .inp(inp), .load(demultiplexer_1_out1), .address(address[5:3]), .outp(main1_1_outp));
  main1 main1_2 (.clck(clck), .inp(inp), .load(demultiplexer_1_out2), .address(address[5:3]), .outp(main1_2_outp));
  main1 main1_3 (.clck(clck), .inp(inp), .load(demultiplexer_1_out3), .address(address[5:3]), .outp(main1_3_outp));
  main1 main1_4 (.clck(clck), .inp(inp), .load(demultiplexer_1_out4), .address(address[5:3]), .outp(main1_4_outp));
  main1 main1_5 (.clck(clck), .inp(inp), .load(demultiplexer_1_out5), .address(address[5:3]), .outp(main1_5_outp));
  main1 main1_6 (.clck(clck), .inp(inp), .load(demultiplexer_1_out6), .address(address[5:3]), .outp(main1_6_outp));
  main1 main1_7 (.clck(clck), .inp(inp), .load(demultiplexer_1_out7), .address(address[5:3]), .outp(main1_7_outp));
  Multiplexer #(.select(3), .width(16)) multiplexer_1 (
    .in0(RAM8_outp), .in1(main1_1_outp), .in2(main1_2_outp), .in3(main1_3_outp), .in4(main1_4_outp),
    .in5(main1_5_outp), .in6(main1_6_outp), .in7(main1_7_outp), .out(out_5), .sel(address[2:0]));

  // Other names for the same wires on the sheet: address_t[2:0] = address[2:0]
endmodule
