// Logisim project RAM8.circ as structural Verilog: 1 circuit, main circuit main1
module main1 (
  input  clck,
  input  [15:0] inp,
  input  load,
  input  [2:0] address,
  output [15:0] outp
);

  wire demultiplexer_1_out0, demultiplexer_1_out1, demultiplexer_1_out2, demultiplexer_1_out3,
       demultiplexer_1_out4, demultiplexer_1_out5, demultiplexer_1_out6, demultiplexer_1_out7;
  wire [15:0] main_1_outp, main_2_outp, main_3_outp, main_4_outp, main_5_outp, main_6_outp, main_7_outp,
       Regs_outp;

  Demultiplexer #(.select(3)) demultiplexer_1 (
    .out0(demultiplexer_1_out0), .out1(demultiplexer_1_out1), .out2(demultiplexer_1_out2),
    .out3(demultiplexer_1_out3), .out4(demultiplexer_1_out4), .out5(demultiplexer_1_out5),
    .out6(demultiplexer_1_out6), .out7(demultiplexer_1_out7), .in(load), .sel(address));
  Register16bit_main Regs (.clck(clck), .inp(inp), .load(demultiplexer_1_out0), .outp(Regs_outp));
  Register16bit_main main_1 (.clck(clck), .inp(inp), .load(demultiplexer_1_out1), .outp(main_1_outp));
  Register16bit_main main_2 (.clck(clck), .inp(inp), .load(demultiplexer_1_out2), .outp(main_2_outp));
  Register16bit_main main_3 (.clck(clck), .inp(inp), .load(demultiplexer_1_out3), .outp(main_3_outp));
  Register16bit_main main_4 (.clck(clck), .inp(inp), .load(demultiplexer_1_out4), .outp(main_4_outp));
  Register16bit_main main_5 (.clck(clck), .inp(inp), .load(demultiplexer_1_out5), .outp(main_5_outp));
  Register16bit_main main_6 (.clck(clck), .inp(inp), .load(demultiplexer_1_out6), .outp(main_6_outp));
  Register16bit_main main_7 (.clck(clck), .inp(inp), .load(demultiplexer_1_out7), .outp(main_7_outp));
  Multiplexer #(.select(3), .width(16)) multiplexer_1 (
    .in0(Regs_outp), .in1(main_1_outp), .in2(main_2_outp), .in3(main_3_outp), .in4(main_4_outp),
    .in5(main_5_outp), .in6(main_6_outp), .in7(main_7_outp), .out(outp), .sel(address));
endmodule
