// Logisim project Xor.circ as structural Verilog: 1 circuit, main circuit main
module main (
);

  wire dipswitch_1_sw1, dipswitch_1_sw2, nand_1_out, nand_2_out, nand_3_out, nand_4_out, nand_5_out,
       nand_6_out, nand_7_out, nand_8_out, nand_9_out;

  DipSwitch #(.number(2)) dipswitch_1 (.sw1(dipswitch_1_sw1), .sw2(dipswitch_1_sw2));
  nand nand_1 (nand_1_out, dipswitch_1_sw1, dipswitch_1_sw1);
  nand nand_2 (nand_2_out, dipswitch_1_sw2, dipswitch_1_sw2);
  nand nand_3 (nand_3_out, nand_1_out, dipswitch_1_sw2);
  nand nand_4 (nand_4_out, dipswitch_1_sw1, nand_2_out);
  nand nand_5 (nand_5_out, nand_3_out, nand_3_out);
  nand nand_6 (nand_6_out, nand_4_out, nand_4_out);
  nand nand_7 (nand_7_out, nand_5_out, nand_5_out);
  nand nand_8 (nand_8_out, nand_6_out, nand_6_out);
  nand nand_9 (nand_9_out, nand_7_out, nand_8_out);
  LED led_1 (.in(nand_9_out));
endmodule
