// Logisim project basic_combinatorial_gates.circ as structural Verilog
module halfAdder (
  input  X,
  input  Y,
  output Sum,
  output Cout
);

  xor xor_1 (Sum, X, Y);
  and and_1 (Cout, X, Y);
endmodule

module FullAdder (
  input  X,
  input  Y,
  input  Cin,
  output Sum,
  output Cout
);

  wire halfadder_1_cout, halfadder_1_sum, halfadder_2_cout;

  halfAdder halfadder_1 (.X(X), .Y(Y), .Sum(halfadder_1_sum), .Cout(halfadder_1_cout));
  halfAdder halfadder_2 (.X(halfadder_1_sum), .Y(Cin), .Sum(Sum), .Cout(halfadder_2_cout));
  or or_1 (Cout, halfadder_2_cout, halfadder_1_cout);
endmodule

module SRLatch (
  input  Set,
  input  Reset,
  output Q,
  output ntQ
);

  nand nand_1 (Q, Set, ntQ);
  nand nand_2 (ntQ, Q, Reset);
endmodule

module tffcounter_7seg (
  input  in_1
);

  wire and_1_out, clock_1_out;
  wire [2:0] t_ff_1_q;

  T_Flip_Flop t_ff_1 (.T(in_1), .clk(clock_1_out), .Q(t_ff_1_q[0]));  // open: Qn, reset, preset
  Clock clock_1 (.out(clock_1_out));
  T_Flip_Flop t_ff_2 (.T(t_ff_1_q[0]), .clk(clock_1_out), .Q(t_ff_1_q[1]));  // open: Qn, reset, preset
  and and_1 (and_1_out, t_ff_1_q[0], t_ff_1_q[1]);
  T_Flip_Flop t_ff_3 (.T(and_1_out), .clk(clock_1_out), .Q(t_ff_1_q[2]));  // open: Qn, reset, preset
  _7_Segment_Display u_7_segment_display_1 ();  // open: g, f, a, b, e, d, c, dp
  // BCD_to_7_Segment_decoder bcd_to_7_segment_decoder_1: pin names not known; wires that end beside it: {1'b0, t_ff_1_q}
endmodule

module \byte  (
  input  clk,
  input  [7:0] inp,
  input  set,
  output [7:0] o
);

  wire and_1_out, and_2_out, and_3_out, and_4_out, and_5_out, and_6_out, and_7_out, and_8_out;

  and and_1 (and_1_out, inp[0], set);
  and and_2 (and_2_out, inp[1], set);
  and and_3 (and_3_out, inp[2], set);
  and and_4 (and_4_out, inp[3], set);
  and and_5 (and_5_out, inp[4], set);
  and and_6 (and_6_out, inp[5], set);
  and and_7 (and_7_out, inp[6], set);
  and and_8 (and_8_out, inp[7], set);
  D_Flip_Flop d_ff_1 (.D(and_1_out), .clk(clk), .Q(o[0]));  // open: Qn, preset, reset
  D_Flip_Flop d_ff_2 (.D(and_2_out), .clk(clk), .Q(o[1]));  // open: Qn, preset, reset
  D_Flip_Flop d_ff_3 (.D(and_3_out), .clk(clk), .Q(o[2]));  // open: Qn, preset, reset
  D_Flip_Flop d_ff_4 (.D(and_4_out), .clk(clk), .Q(o[3]));  // open: Qn, preset, reset
  D_Flip_Flop d_ff_5 (.D(and_5_out), .clk(clk), .Q(o[4]));  // open: Qn, preset, reset
  D_Flip_Flop d_ff_6 (.D(and_6_out), .clk(clk), .Q(o[5]));  // open: Qn, preset, reset
  D_Flip_Flop d_ff_7 (.D(and_7_out), .clk(clk), .Q(o[6]));  // open: Qn, preset, reset
  D_Flip_Flop d_ff_8 (.D(and_8_out), .clk(clk), .Q(o[7]));  // open: Qn, preset, reset
endmodule

module basicdecoder (
  input  A,
  input  B,
  output D0,
  output D1,
  output D2,
  output D3
);

  wire not_1_out, not_2_out;

  not not_1 (not_1_out, A);
  not not_2 (not_2_out, B);
  and and_1 (D0, not_1_out, not_2_out);
  and and_2 (D1, not_1_out, B);
  and and_3 (D2, A, not_2_out);
  and and_4 (D3, A, B);
endmodule

module counter_tff (
  input  set,
  input  clk,
  output [2:0] out_3
);

  wire and_1_out;

  T_Flip_Flop t_ff_1 (.T(set), .clk(clk), .Q(out_3[0]));  // open: Qn, reset, preset
  T_Flip_Flop t_ff_2 (.T(out_3[0]), .clk(clk), .Q(out_3[1]));  // open: Qn, reset, preset
  and and_1 (and_1_out, out_3[0], out_3[1]);
  T_Flip_Flop t_ff_3 (.T(and_1_out), .clk(clk), .Q(out_3[2]));  // open: Qn, reset, preset
endmodule

module rudimentary_counter (
);

  wire clock_1_out, switch_1_p2;
  wire [2:0] counter_tff_1_out_3;
  wire [7:0] byte_1_o, decoder_1_out0;

  // Switch switch_1: pin names not known; wires that end beside it: 1'b1, switch_1_p2
  Clock clock_1 (.out(clock_1_out));
  counter_tff counter_tff_1 (.set(switch_1_p2), .clk(clock_1_out), .out_3(counter_tff_1_out_3));
  Decoder #(.select(3)) decoder_1 (
    .out0(decoder_1_out0[0]), .out1(decoder_1_out0[1]), .out2(decoder_1_out0[2]), .out3(decoder_1_out0[3]),
    .out4(decoder_1_out0[4]), .out5(decoder_1_out0[5]), .out6(decoder_1_out0[6]), .out7(decoder_1_out0[7]),
    .sel(counter_tff_1_out_3), .en(switch_1_p2));
  LED led_1 (.in(decoder_1_out0[0]));
  LED led_2 (.in(decoder_1_out0[1]));
  LED led_3 (.in(decoder_1_out0[2]));
  LED led_4 (.in(decoder_1_out0[3]));
  LED led_5 (.in(decoder_1_out0[4]));
  LED led_6 (.in(decoder_1_out0[5]));
  LED led_7 (.in(decoder_1_out0[6]));
  LED led_8 (.in(decoder_1_out0[7]));
  \byte  byte_1 (.clk(clock_1_out), .inp(decoder_1_out0), .set(switch_1_p2), .o(byte_1_o));
  // LedBar #(.inputtype("row")) ledbar_1: pin names not known; wires that end beside it: byte_1_o
endmodule

module cmp_1bit (
  input  a,
  input  b,
  output b_larger,
  output equal,
  output a_larger
);

  wire not_1_out, not_2_out;

  not not_1 (not_1_out, a);
  not not_2 (not_2_out, b);
  and and_1 (b_larger, not_1_out, b);
  and and_2 (a_larger, a, not_2_out);
  xnor xnor_1 (equal, b_larger, a_larger);
endmodule

module ram_experiment (
  input  [7:0] in_1,
  input  in_2,
  input  in_3
);

  wire clock_1_out;
  wire [7:0] byte_1_o, ram_1_dout;

  Clock clock_1 (.out(clock_1_out));
  \byte  byte_1 (.clk(clock_1_out), .inp(in_1), .set(in_2), .o(byte_1_o));
  RAM ram_1 (.addr(byte_1_o), .we(in_2), .oe(in_3), .clk(clock_1_out), .din(byte_1_o), .dout(ram_1_dout));
endmodule

module cmp_2bit (
  input  [1:0] a,
  input  [1:0] b,
  output equal,
  output a_larger,
  output b_larger
);

  wire and_1_out, and_2_out;
  wire [1:0] cmp_1bit_1_a_larger, cmp_1bit_1_b_larger, cmp_1bit_1_equal;

  cmp_1bit cmp_1bit_1 (
    .a(a[0]), .b(b[0]), .b_larger(cmp_1bit_1_b_larger[0]), .equal(cmp_1bit_1_equal[0]),
    .a_larger(cmp_1bit_1_a_larger[0]));
  cmp_1bit cmp_1bit_2 (
    .a(a[1]), .b(b[1]), .b_larger(cmp_1bit_1_b_larger[1]), .equal(cmp_1bit_1_equal[1]),
    .a_larger(cmp_1bit_1_a_larger[1]));
  and and_1 (and_1_out, cmp_1bit_1_a_larger[0], cmp_1bit_1_equal[1]);
  and and_2 (and_2_out, cmp_1bit_1_equal[1], cmp_1bit_1_b_larger[0]);
  and and_3 (equal, cmp_1bit_1_equal[0], cmp_1bit_1_equal[1]);
  or or_1 (a_larger, and_1_out, cmp_1bit_1_a_larger[1]);
  or or_2 (b_larger, cmp_1bit_1_b_larger[1], and_2_out);
endmodule

module cmp_4bit (
  input  [3:0] a,
  input  [3:0] b,
  output equal,
  output a_larger,
  output b_larger
);

  wire and_1_out, and_2_out, cmp_2bit_1_a_larger, cmp_2bit_1_b_larger, cmp_2bit_1_equal, cmp_2bit_2_a_larger,
       cmp_2bit_2_b_larger, cmp_2bit_2_equal;

  cmp_2bit cmp_2bit_1 (
    .a(a[1:0]), .b(b[1:0]), .equal(cmp_2bit_1_equal), .a_larger(cmp_2bit_1_a_larger),
    .b_larger(cmp_2bit_1_b_larger));
  cmp_2bit cmp_2bit_2 (
    .a(a[3:2]), .b(b[3:2]), .equal(cmp_2bit_2_equal), .a_larger(cmp_2bit_2_a_larger),
    .b_larger(cmp_2bit_2_b_larger));
  and and_1 (and_1_out, cmp_2bit_2_equal, cmp_2bit_1_a_larger);
  and and_2 (and_2_out, cmp_2bit_2_equal, cmp_2bit_1_b_larger);
  and and_3 (equal, cmp_2bit_1_equal, cmp_2bit_2_equal);
  or or_1 (a_larger, and_1_out, cmp_2bit_2_a_larger);
  or or_2 (b_larger, cmp_2bit_2_b_larger, and_2_out);
endmodule
